# Fritzing sketch wiring-1-board-bme280-notecard (saved by Fritzing 1.0.0)

parts:
  Board = LilyGO T-Display-S3 AMOLED 1.91
  BT1 = Board LiPo
  U1 = BME280 0x76
  U2 = Notecarrier-X + Notecard MBGLW
  BT2 = Notecarrier LiPo

nets:
  N1: Board.GND_R1, U1.GND
  N2: Board.IO44, U1.SCL
  N3: Board.IO43, U1.SDA
  N4: Board.3V3_R1, U1.VIN
  N5: Board.BAT-, BT1.-
  N6: Board.BAT+, BT1.+
  N7: Board.Q_GND, U2.GND
  N8: Board.Q_SDA, U2.SDA
  N9: Board.Q_SCL, U2.SCL
  N10: U2.BAT-, BT2.-
  N11: U2.BAT+, BT2.+

notes:
  Board, battery, BME280 (FSD 23, on main), cellular (FSD 33, not built)
  BME280 at 0x76 on SDA GPIO 43 / SCL GPIO 44, 3.3 V. The keys (GPIO 0, 21)
  and the green LED (GPIO 38) are on the board: nothing to wire.
  Notecarrier-X by a Qwiic cable (I2C 0x17), GND, SDA and SCL only: its 3.3 V
  wire stays unconnected, and its own LiPo feeds the Notecard and the modem.
  Title bars: green = firmware on main; blue = in the FSD, not built yet;
  orange = proposed, not in the FSD.
  Generated by make_wiring.py, 2026-11-02 (US Eastern).

custom parts:
  LilyGO T-Display-S3 AMOLED 1.91: LilyGO T-Display-S3 AMOLED 1.91 inch (ESP32-S3R8), header pins as on LilyGO's pinout picture, seen from the chip side.
  BME280 0x76: BME280 breakout (I2C 0x76)
  Notecarrier-X + Notecard MBGLW: Blues Notecarrier-X v1.3 with Notecard Cell+WiFi NOTE-MBGLW v2.5
