# Fritzing sketch wiring-10-outdoor-node (saved by Fritzing 1.0.0)

parts:
  PoE = PoE+ injector TP-Link TL-PoE160S
  SP = Surge protector Ubiquiti ETH-SP-G2
  PE = House ground bonding conductor
  SPL = PoE+ splitter PLANET POE-162S
  BA = Buck 12 -> 5.1 V 3 A, USB-C out
  BB = Buck 12 -> 5.1 V 3 A, USB-C out
  Pi = Raspberry Pi 4 B harness, AP tds3-bench
  Hub = UUGear MEGA4 per-port power (uhubctl)
  R1 = Resistor 1k
  R2 = Resistor 1k
  DUT = T-Display-S3 AMOLED DUT, SLOT1, battery fitted

nets:
  N1: PoE.PoE+_out, SP.in
  N2: SP.out, SPL.PoE+_in
  N3: SP.GND_lug, PE.PE
  N4: SPL.LAN_out, Pi.Ethernet
  N5: SPL.12_V_+, BA.VIN+, BB.VIN+
  N6: SPL.12_V_-, BA.VIN-, BB.VIN-
  N7: BA.5.1_V_out, Pi.USB-C_power
  N8: BB.5.1_V_out, Hub.USB-C_power
  N9: Pi.USB_3_port, Hub.upstream
  N10: Pi.pin_11_BCM_17, R1.1
  N11: Pi.pin_12_BCM_18, R2.1
  N12: Pi.pin_14_GND, DUT.GND
  N13: Hub.port_1, DUT.USB-C
  N14: R1.2, DUT.RESET_key_pad
  N15: R2.2, DUT.BOOT_key_pad

notes:
  Outdoor test node (docs/Method/project/outdoor-node.md): test rig, not product wiring
  Green: one outdoor shielded Cat6 (<= 100 m) with 802.3at power; the surge protector's lug on the house ground.
  The splitter's 12 V feeds two 5.1 V converters: one for the Pi, one for the MEGA4, so DUT and modem bursts
  stay off the Pi's rail. The MEGA4 switches each port's power (uhubctl): port 1 is the DUT's reset and detached mode.
  Pi header pin 11 (BCM 17) -> 1k -> RESET key pad (EN); pin 12 (BCM 18) -> 1k -> BOOT key pad (GPIO 0); pin 14 GND.
  The BME280 (radiation shield) and the Notecarrier are wired as on sheets 1 and 9; antennas outside the lid.
  Build steps and checks: outdoor-node-build.md. Title bars: green = firmware on main; blue = in the FSD, not built yet; orange = proposed, not in the FSD.
  Generated by make_wiring.py, 2026-11-02 (US Eastern).

custom parts:
  PoE+ injector TP-Link TL-PoE160S: PoE+ injector, IEEE 802.3at, gigabit (TP-Link TL-PoE160S)
  Surge protector Ubiquiti ETH-SP-G2: Shielded gigabit Ethernet surge protector with ground lug (Ubiquiti ETH-SP-G2)
  House ground bonding conductor: The building's protective earth, where the surge protector is bonded
  PoE+ splitter PLANET POE-162S: 802.3at PoE+ splitter, 12 V 2 A DC out, gigabit (PLANET POE-162S)
  Buck 12 -> 5.1 V 3 A, USB-C out: Step-down converter 12 V to 5.1 V 3 A with a USB-C output lead
  Raspberry Pi 4 B harness, AP tds3-bench: Raspberry Pi 4 Model B running the Embedded AI Harness (the outdoor node)
  UUGear MEGA4 per-port power (uhubctl): UUGear MEGA4 4-port USB 3.1 hub with per-port power switching
  T-Display-S3 AMOLED DUT, SLOT1, battery fitted: The DUT: LilyGO T-Display-S3 AMOLED on its carrier, wired to the node's RESET and BOOT key pads
