# Fritzing sketch wiring-11-fs3-core (saved by Fritzing 1.0.0)

parts:
  Board = Unexpected Maker FeatherS3D
  J1 = Bench lines via Schottky diodes
  BT1 = FeatherS3 LiPo
  R1 = Resistor 10k
  SW1 = User key momentary, NO
  U1 = BME280 STEMMA QT, 0x76
  U2 = Analog board ISO1540 side 1 (sheet 13)
  U3 = RV-8803 RTC Adafruit 6538, 0x32
  U4 = Notecarrier-X + Notecard, 0x17
  BT2 = Notecarrier LiPo

nets:
  N1: Board.RST, J1.RST
  N2: Board.IO0, J1.IO0
  GND: Board.GND, J1.GND, SW1.COM, U1.GND, U2.GND1, U3.GND, U4.GND
  N3: Board.IO1, R1.1, SW1.NO
  N4: Board.SCL15, U1.SCL, U2.SCL1
  N5: Board.SDA16, U1.SDA, U2.SDA1
  N6: Board.LDO2, U1.3V3, U2.VCC1
  N7: Board.SCL9, U3.SCL, U4.SCL
  N8: Board.SDA8, U3.SDA, U4.SDA
  3V3: Board.3V3, R1.2, U3.3V3
  N9: Board.BAT-, BT1.-
  N10: Board.BAT+, BT1.+
  N11: U4.BAT-, BT2.-
  N12: U4.BAT+, BT2.+

notes:
  FeatherS3D build: power, both buses, key and bench lines (FSD 40.2)
  The board in its header order, USB-C up; the STEMMA QT sockets' pins are drawn on its bottom edge.
  Always-on bus (I2C1 STEMMA, LDO1): the board's MAX17048 0x36, RV-8803 0x32 and the Notecarrier-X
  0x17, its red 3.3 V wire unconnected and its own LiPo. Daisy-chain through the RTC's second port.
  Switched bus (I2C2 STEMMA, LDO2, off in deep sleep): BME280 0x76 and the analog board's isolator
  (sheet 13); SDA is GPIO 16, SCL GPIO 15. User key GPIO 1 to GND, 10k pull-up to 3V3.
  Bench RST and GPIO 0 only through the diodes of sheet 16 (C-40.9). Each LiPo charges from its own USB-C.
  Title bars: green = firmware on main; blue = in the FSD, not built yet; orange = proposed, not in the FSD.

custom parts:
  Unexpected Maker FeatherS3D: Unexpected Maker FeatherS3D (ESP32-S3), top view with USB-C up: both headers in their physical order, the STEMMA QT sockets' pins at the bottom.
  Bench lines via Schottky diodes: The bench slot's RST and GPIO 0 lines, each through a Schottky diode (FSD C-40.9, sheet 16)
  User key momentary, NO: Momentary user key, normally open
  BME280 STEMMA QT, 0x76: BME280 breakout on STEMMA QT (I2C 0x76)
  Analog board ISO1540 side 1 (sheet 13): The analog board's I2C isolator, board side (sheet 13)
  RV-8803 RTC Adafruit 6538, 0x32: Adafruit RV-8803 RTC breakout (6538), STEMMA QT, I2C 0x32
  Notecarrier-X + Notecard, 0x17: Blues Notecarrier-X with Notecard on STEMMA QT, its own LiPo
