# Fritzing sketch wiring-13-fs3-analog (saved by Fritzing 1.0.0)

parts:
  Board = Unexpected Maker FeatherS3D
  U2 = Load switch
  U3 = Converter -> 5 V
  U4 = Iso DC-DC 24 V 2 W, 3 kV
  U9 = Limit 30 mA
  U6 = 4-20 mA transmitter
  D1 = TVS diode P6KE33A
  R2 = Shunt resistor 100R 0.1%
  U5 = LDO 3.3 V (iso)
  U7 = ADS1115 Adafruit 1085 0x49
  U8 = I2C isolator Adafruit 4903 side 2 | side 1
  R1 = Resistor 100k
  P1 = Level probe EALLT-1, 0-5 V
  R3 = Resistor 15k 0.1%
  R4 = Resistor 10k 0.1%

nets:
  GND: Board.GND, U2.GND, U3.GND, U4.-VIN, U8.GND1, R1.2
  N1: Board.IO18, U2.ON, R1.1
  N2: Board.VBAT, U2.VIN
  N3: Board.SCL15, U8.SCL1
  N4: Board.SDA16, U8.SDA1
  N5: Board.LDO2, U8.VCC1
  N6: U2.VOUT, U3.VIN
  N7: U3.VOUT, U4.+VIN
  N8: U4.+VO, U9.IN, U5.IN, P1.+V
  GND_2: U4.0V, R2.2, U5.GND, U7.A1, U7.GND, U8.GND2, P1.0V, R4.2
  N9: U9.OUT, U6.+, D1.K
  N10: U6.-, D1.A, R2.1, U7.A0
  N11: U5.OUT, U7.VDD, U7.ADDR, U8.VCC2
  N12: U7.A2, R3.2, R4.1
  N13: U7.SCL, U8.SCL2
  N14: U7.SDA, U8.SDA2
  N15: P1.OUT, R3.1

notes:
  FeatherS3D build: the analog board, 4-20 mA loop and 0-5 V level probe (FSD 29, 40.2, FR-40.9)
  GPIO 18 high switches the supply on from VBAT; the 100k holds it off through sleep and reset. The isolated
  24 V (2 W, 3 kV) feeds the loop through the 30 mA limit and the level probe; grey (0V iso) and purple (24 V)
  never touch the board's ground. Loop: A0 - A1 across the 100 R shunt. Probe: OUT -> 15k -> A2, 10k A2 to 0V iso
  (x 2.5, A2 single-ended at +/-2.048 V). One channel is read at a time (loop in or volt). The isolator's side 1
  is on the switched bus (the I2C2 STEMMA QT, sheet 11). Field cables enter through the surge protectors of sheet 15.
  Title bars: green = firmware on main; blue = in the FSD, not built yet; orange = proposed, not in the FSD.

custom parts:
  Unexpected Maker FeatherS3D: Unexpected Maker FeatherS3D (ESP32-S3), top view with USB-C up: both headers in their physical order, the STEMMA QT sockets' pins at the bottom.
  Load switch: Load switch for the loop supply: DMG2305UX P-MOSFET on a SOT-23 breakout, driven by a 2N3904
  Converter -> 5 V: Pololu S7V8F5 step-up/step-down to 5 V, feeding the isolated DC-DC
  Iso DC-DC 24 V 2 W, 3 kV: Isolated DC-DC, 5 V in, 24 V out, 2 W, at least 3 kV isolation (FSD 40.2)
  Limit 30 mA: Loop current limit DN2540N3, about 30 mA
  4-20 mA transmitter: 2-wire 4-20 mA transmitter on the loop terminals
  LDO 3.3 V (iso): onsemi LM317LZG regulator for the isolated side's 3.3 V
  ADS1115 Adafruit 1085 0x49: ADS1115 for the 4-20 mA loop, address 0x49
  I2C isolator Adafruit 4903 side 2 | side 1: I2C isolator, side 1 on the board's bus
  Level probe EALLT-1, 0-5 V: Earu EALLT-1 submersible level transmitter, 0 - 5 m, 0 - 5 V, 10 - 30 V supply
