# Fritzing sketch wiring-15-fs3-entry (saved by Fritzing 1.0.0)

parts:
  W1 = Field cable shielded twisted pair
  SP1 = Surge protector GDT, series R/PTC, TVS
  T1 = Isolated board field terminals
  E1 = Earth rod one per station

nets:
  N1: W1.wire_1, SP1.L1_in
  N2: W1.wire_2, SP1.L2_in
  N3: W1.wire_3, SP1.L3_in
  N4: W1.wire_4, SP1.L4_in
  N5: W1.shield, SP1.EARTH, E1.rod
  N6: SP1.L1_out, T1.T1
  N7: SP1.L2_out, T1.T2
  N8: SP1.L3_out, T1.T3
  N9: SP1.L4_out, T1.T4

notes:
  FeatherS3D build: each field cable's entry (FSD C-40.5 - C-40.8)
  Every field line (the loop pair, the probe's three wires, the MaxBotix's four) passes a
  protector at the enclosure wall: a gas discharge tube to earth, then a series resistor
  or PTC, then a TVS sized for its line (24 V supplies, 5 V signals). The protectors share
  one earth rod by a short, heavy conductor. The shield is bonded at this end only.
  Then the isolated board (sheet 13 or 14): 3 kV between the field and the board's ground.
  Title bars: green = firmware on main; blue = in the FSD, not built yet; orange = proposed, not in the FSD.

custom parts:
  Field cable shielded twisted pair: A field cable: up to four conductors and an overall shield
  Surge protector GDT, series R/PTC, TVS: Surge protector per line: gas discharge tube to earth, series resistor or PTC, TVS (FSD C-40.7)
  Isolated board field terminals: The field terminals of the analog board or the serial port
  Earth rod one per station: The station's earth rod, bonded by a short heavy conductor
