# Fritzing sketch wiring-16-fs3-bench (saved by Fritzing 1.0.0)

parts:
  Board = Unexpected Maker FeatherS3D
  Pi = Raspberry Pi 40-pin header
  D1 = Schottky diode 1N5711
  D2 = Schottky diode 1N5711

nets:
  N1: Board.RST, D1.A
  N2: Board.IO0, D2.A
  N3: Board.GND, Pi.pin_14
  N4: Pi.pin_11, D1.K
  N5: Pi.pin_12, D2.K

notes:
  FeatherS3D: the bench's BOOT and RST lines (FSD C-40.9)
  Both drawn as on the boards. Pi: pair 1 is EN pin 11 (BCM 17), BOOT pin 12 (BCM 18), GND pin 14.
  For another slot move both wires to its pair: 2 = pins 15/16, 3 = pins 18/22, 4 = pins 37/13;
  the nearest GND is any grey pin. Never pins 3, 5, 29, 31, 32, 33 (the signal generator).
  FeatherS3D, long header: RST the first pin, 3V3.1 the second (no wire), GPIO 0 the third (0),
  GND the fourth. D1, D2: 1N5711 or BAT43 Schottky, band (cathode) at the Pi: Pi low pulls the
  pin to about 0.4 V, Pi high is blocked. The Pi's default 50k pull-down on BCM 17 holds the
  board in reset through D1: add gpio=17,18=ip,pu to /boot/firmware/config.txt (that pair's
  pins for another slot). Then set the slot's gpio_en / gpio_boot, restart the portal and run
  the BOOT/EN test with the board awake.
  Title bars: green = firmware on main; blue = in the FSD, not built yet; orange = proposed, not in the FSD.

custom parts:
  Unexpected Maker FeatherS3D: Unexpected Maker FeatherS3D (ESP32-S3), top view with USB-C up: both headers in their physical order, the STEMMA QT sockets' pins at the bottom.
  Raspberry Pi 40-pin header: Raspberry Pi 4 40-pin GPIO header in its physical layout, with the testbench's slot GPIO pairs marked
