# Fritzing sketch wiring-2-loop-4-20ma (saved by Fritzing 1.0.0)

parts:
  Board = LilyGO T-Display-S3 AMOLED 1.91
  U2 = Load switch
  U3 = Converter -> 5 V
  U4 = Iso DC-DC 24 V
  U9 = Limit 30 mA
  U6 = 4-20 mA transmitter
  D1 = TVS diode P6KE33A
  R2 = Shunt resistor 100R 0.1%
  U5 = LDO 3.3 V (iso)
  U7 = ADS1115 Adafruit 1085 0x49
  U8 = I2C isolator Adafruit 4903 side 2 | side 1
  R1 = Resistor 100k

nets:
  N1: Board.IO3, U2.ON, U8.VCC1, R1.1
  N2: Board.IO15, U8.SDA1
  GND: Board.GND, U2.GND, U3.GND, U4.-VIN, U8.GND1, R1.2
  N3: Board.VSYS, U2.VIN
  N4: Board.IO16, U8.SCL1
  N5: U2.VOUT, U3.VIN
  N6: U3.VOUT, U4.+VIN
  N7: U4.+VO, U9.IN, U5.IN
  GND_2: U4.0V, R2.2, U5.GND, U7.A1, U7.GND, U8.GND2
  N8: U9.OUT, U6.+, D1.K
  N9: U6.-, D1.A, R2.1, U7.A0
  N10: U5.OUT, U7.VDD, U7.ADDR, U8.VCC2
  N11: U7.SCL, U8.SCL2
  N12: U7.SDA, U8.SDA2

notes:
  4-20 mA loop input (FSD 29) - firmware on main
  GPIO 3 high switches the loop supply on (soft-start load switch) and powers isolator side 1; the 100k holds it
  off through sleep and reset. The loop ADS1115 has its own I2C bus on GPIO 15/16, floating while the loop is off.
  VSYS is the battery/system rail. Grey (0V iso) and purple (24 V) are the isolated side: they never touch
  the board's ground. The 30 mA limit keeps a shorted loop under 3 V on the shunt (100 R 0.1 %: 0.4 V at 4 mA,
  2.0 V at 20 mA, read as A0 - A1 at +/-4.096 V). The LDO feeds the ADS1115 and isolator side 2 from 24 V.
  Title bars: green = firmware on main; blue = in the FSD, not built yet; orange = proposed, not in the FSD.

custom parts:
  LilyGO T-Display-S3 AMOLED 1.91: LilyGO T-Display-S3 AMOLED 1.91 inch (ESP32-S3R8), header pins as on LilyGO's pinout picture, seen from the chip side.
  Load switch: Load switch for the loop supply: DMG2305UX P-MOSFET on a SOT-23 breakout, driven by a 2N3904
  Converter -> 5 V: Pololu S7V8F5 step-up/step-down to 5 V, feeding the isolated DC-DC
  Iso DC-DC 24 V: Isolated 1 W DC-DC Mornsun B0524S-1WR3, 24 V out
  Limit 30 mA: Loop current limit DN2540N3, about 30 mA
  4-20 mA transmitter: 2-wire 4-20 mA transmitter on the loop terminals
  LDO 3.3 V (iso): onsemi LM317LZG regulator for the isolated side's 3.3 V
  ADS1115 Adafruit 1085 0x49: ADS1115 for the 4-20 mA loop, address 0x49
  I2C isolator Adafruit 4903 side 2 | side 1: I2C isolator, side 1 on the board's bus
