# Fritzing sketch wiring-3-water-probe (saved by Fritzing 1.0.0)

parts:
  Board = LilyGO T-Display-S3 AMOLED 1.91
  BT1 = Board LiPo
  R3 = Resistor 100k
  U9 = ADS1115 water 0x48
  C1 = Capacitor 100 nF
  R6 = Resistor 1k
  D1 = Schottky diode 1N5711
  D2 = Schottky diode 1N5711
  R4 = Resistor 10k 0.1%
  R5 = Resistor 10k 0.1%
  U11 = Pressure probe 0.5-4.5 V ratiometric
  C3 = Capacitor 10 uF
  C4 = Capacitor 100 nF
  R9 = Resistor 1k
  C2 = Capacitor 100 nF
  R7 = Resistor 10k 0.1%
  R8 = Resistor 10k 0.1%
  U10 = MiniBoost 5V Adafruit 4654
  F1 = Fuse 1 A

nets:
  N1: Board.3V3, D1.K
  N2: Board.IO2, R3.1, U10.EN
  N3: Board.GND, R3.2
  GND: Board.GND_R1, U9.ADDR, U9.GND, C1.2, D2.A, R5.2, U11.GND, C3.2, C4.2, C2.2, R8.2, U10.GND
  N4: Board.IO44, U9.SCL
  N5: Board.IO43, U9.SDA
  N6: Board.3V3_R1, U9.VDD
  N7: Board.BAT-, BT1.-
  N8: Board.BAT+, BT1.+, F1.1
  N9: U9.A0, C1.1, R6.1
  N10: U9.A1, R9.1, C2.1
  N11: R6.2, D1.A, D2.K, R4.1, R5.1
  N12: R4.2, U11.OUT
  +5V: U11.+5V, C3.1, C4.1, R7.1, U10.5V
  N13: R9.2, R7.2, R8.1
  N14: U10.VIN, F1.2

notes:
  Water pressure probe - proposed, not in the FSD (docs/Method/project/water-probe-circuit.md)
  GPIO 2 high switches the boost on; the 100k holds EN low through sleep and reset. VIN taps the
  battery at its connector through a 1 A fuse. ADS1115 ADDR to GND gives 0x48.
  Probe: OUT -> 10k -> node -> 10k -> GND; node -> 1k -> A0, 100 nF A0-GND; D1 node to 3V3, D2 GND to node.
  Reference: boost 5 V -> 10k -> node -> 10k -> GND; node -> 1k -> A1, 100 nF A1-GND. Resistors 0.1 %, matched.
  Title bars: green = firmware on main; blue = in the FSD, not built yet; orange = proposed, not in the FSD.

custom parts:
  LilyGO T-Display-S3 AMOLED 1.91: LilyGO T-Display-S3 AMOLED 1.91 inch (ESP32-S3R8), header pins as on LilyGO's pinout picture, seen from the chip side.
  ADS1115 water 0x48: ADS1115 for the water probe, address 0x48
  Pressure probe 0.5-4.5 V ratiometric: Ratiometric 0.5-4.5 V pressure probe
  MiniBoost 5V Adafruit 4654: Adafruit MiniBoost 5V 1A (4654)
