# Fritzing sketch wiring-4-rs232 (saved by Fritzing 1.0.0)

parts:
  Board = LilyGO T-Display-S3 AMOLED 1.91
  U12 = MAX3232ECPE+ PDIP-16, pin 1 top left
  C1 = Capacitor 100 nF
  C2 = Capacitor 100 nF
  C3 = Capacitor 100 nF
  C4 = Capacitor 100 nF
  C5 = Capacitor 100 nF
  R10 = Resistor 100k
  J1 = DE-9 male (DTE)
  J2 = Screw terminal 3-pin 5.08 mm

nets:
  N1: Board.IO11, U12.11_T1IN
  N2: Board.IO12, U12.12_R1OUT
  N3: Board.IO13, U12.16_VCC, C5.2, R10.1
  GND: Board.GND, U12.15_GND, U12.10_T2IN, C3.2, C4.2, C5.1, R10.2, J1.5_GND, J2.GND
  N4: U12.1_C1+, C1.2
  N5: U12.2_V+, C3.1
  N6: U12.3_C1-, C1.1
  N7: U12.4_C2+, C2.1
  N8: U12.5_C2-, C2.2
  N9: U12.6_V-, C4.1
  N10: U12.7_T2OUT, J1.7_RTS
  N11: U12.14_T1OUT, J1.3_TXD, J2.TX
  N12: U12.13_R1IN, J1.2_RXD, J2.RX

notes:
  RS232 instrument (FSD 30) - specified, not built
  GPIO 13 is the MAX3232's VCC: it draws nothing while the port is off; R10 (100k) holds it low through sleep and
  reset. UART1: GPIO 11 TX to T1IN (11), GPIO 12 RX from R1OUT (12); both float while off. C1 - C5 are 0.1 uF ceramic.
  J1 DE-9 male (DTE): pin 3 TXD, pin 2 RXD, pin 5 GND, pin 7 RTS (optional: T2IN at GND holds it asserted). J2 is the
  bare-wire alternative. R2IN (8) and R2OUT (9) stay open. Parts and checks in rs232-circuit.md.
  Title bars: green = firmware on main; blue = in the FSD, not built yet; orange = proposed, not in the FSD.

custom parts:
  LilyGO T-Display-S3 AMOLED 1.91: LilyGO T-Display-S3 AMOLED 1.91 inch (ESP32-S3R8), header pins as on LilyGO's pinout picture, seen from the chip side.
  MAX3232ECPE+ PDIP-16, pin 1 top left: RS232 transceiver MAX3232 (PDIP-16) in a DIP socket
  DE-9 male (DTE): DE-9 male connector, DTE, panel mount
  Screw terminal 3-pin 5.08 mm: 3-pin screw terminal, 5.08 mm
