# Fritzing sketch wiring-5-blues-cellular (saved by Fritzing 1.0.0)

parts:
  Board = LilyGO T-Display-S3 AMOLED 1.91
  U2 = Notecarrier-X v1.3 + Notecard NOTE-MBGLW v2.5
  AE1 = LTE antenna flexible, u.FL
  BT2 = Notecarrier LiPo
  AE2 = GPS antenna optional, gps on

nets:
  N1: Board.Q_GND, U2.GND
  N2: Board.Q_SDA, U2.SDA
  N3: Board.Q_SCL, U2.SCL
  N4: U2.MAIN, AE1.u.FL
  N5: U2.GPS, AE2.u.FL
  N6: U2.BAT-, BT2.-
  N7: U2.BAT+, BT2.+

notes:
  Blues cellular uplink (FSD 33) - specified, not built
  Qwiic cable from the board (or the carrier's Qwiic socket) to the Notecarrier-X:
  GND, SDA GPIO 43 and SCL GPIO 44 only. The cable's 3V3 wire and the Notecarrier's
  3V3 pin stay unconnected. The Notecarrier's own LiPo (2000 mAh or more, JST-PH)
  or its USB-C feeds the Notecard and the modem peaks of up to about 2 A.
  Fit the LTE antenna on MAIN before power-up. WIFI stays empty (cellular only,
  FR-33.14). The GPS antenna is fitted only with gps on, for a fix during the
  setup check (FR-33.15). Parts, budgets and checks in blues-cellular.md.
  Title bars: green = firmware on main; blue = in the FSD, not built yet; orange = proposed, not in the FSD.

custom parts:
  LilyGO T-Display-S3 AMOLED 1.91: LilyGO T-Display-S3 AMOLED 1.91 inch (ESP32-S3R8), header pins as on LilyGO's pinout picture, seen from the chip side.
  Notecarrier-X v1.3 + Notecard NOTE-MBGLW v2.5: Blues Notecarrier-X v1.3 with Notecard Cell+WiFi NOTE-MBGLW v2.5: Qwiic, u.FL antenna ports, USB-C, JST-PH LiPo
  LTE antenna flexible, u.FL: Flexible LTE antenna with a u.FL lead, on the Notecard's MAIN port
  GPS antenna optional, gps on: GPS antenna with a u.FL lead, on the Notecard's GPS port (optional)
