# Fritzing sketch wiring-6-blues-cellular-direct (saved by Fritzing 1.0.0)

parts:
  Board = LilyGO T-Display-S3 AMOLED 1.91
  U2 = Notecarrier-X v1.3 + Notecard NOTE-MBGLW v2.5
  AE1 = LTE antenna flexible, u.FL
  AE2 = GPS antenna optional, gps on
  BT2 = Notecarrier LiPo

nets:
  N1: Board.GND_R1, U2.GND, BT2.-
  N2: Board.IO44, U2.SCL
  N3: Board.IO43, U2.SDA
  N4: U2.MAIN, AE1.u.FL
  N5: U2.GPS, AE2.u.FL
  N6: U2.VBAT, BT2.+

notes:
  Blues cellular uplink, direct wiring (FSD 33.2) - specified, not built
  The alternative to sheet 5: no Qwiic cable. Three wires soldered from the carrier's
  I2C fan-out (drawn from the header pins) to the Notecarrier-X header: GND, SDA GPIO 43,
  SCL GPIO 44. VIO, ATTN and every other header pin stay unconnected.
  The LiPo may be soldered to VBAT and GND instead of the JST-PH (or stay on the JST-PH).
  LTE antenna on MAIN; the GPS antenna only with gps on. Checks in blues-cellular.md.
  Title bars: green = firmware on main; blue = in the FSD, not built yet; orange = proposed, not in the FSD.

custom parts:
  LilyGO T-Display-S3 AMOLED 1.91: LilyGO T-Display-S3 AMOLED 1.91 inch (ESP32-S3R8), header pins as on LilyGO's pinout picture, seen from the chip side.
  Notecarrier-X v1.3 + Notecard NOTE-MBGLW v2.5: Blues Notecarrier-X v1.3 with Notecard NOTE-MBGLW v2.5, wired at its 16-pin header instead of Qwiic and JST-PH
  LTE antenna flexible, u.FL: Flexible LTE antenna with a u.FL lead, on the Notecard's MAIN port
  GPS antenna optional, gps on: GPS antenna with a u.FL lead, on the Notecard's GPS port (optional)
