# Fritzing sketch wiring-7-ws-displays (saved by Fritzing 1.0.0)

parts:
  Board = Waveshare ESP32-S3-SIM7670G-4G
  EPD = 4.2in e-Paper Module V2 SSD1683, 8-pin
  OLED = 3.12in OLED Ver 2.1 SSD1322, 4-wire SPI
  R1 = Resistor 10k

nets:
  N1: Board.IO1, EPD.BUSY
  N2: Board.IO3, EPD.CS
  N3: Board.IO19, OLED.RES
  N4: Board.IO20, EPD.RST
  5V: Board.5V, OLED.VCC
  3V3: Board.3V3, EPD.VCC
  GND: Board.GND_R, EPD.GND, OLED.GND, R1.2
  N5: Board.IO7, EPD.CLK, OLED.SCLK
  N6: Board.IO8, EPD.DIN, OLED.SDIN
  N7: Board.IO9, OLED.CS, R1.1
  N8: Board.IO10, EPD.DC, OLED.DC

notes:
  Both displays on the Waveshare board (FSD 35.2, 36, FR-35.25)
  SPI2: CLK GPIO 7, MOSI GPIO 8 and DC GPIO 10 go to both displays; each has its own
  chip select: e-paper CS GPIO 3, OLED CS GPIO 9. E-paper BUSY GPIO 1, RST GPIO 20;
  OLED RES GPIO 19. R1 (10k, CS to GND) tells the firmware the OLED is plugged in;
  the e-paper is found by its BUSY pulse. OLED: R5 + R8 fitted (4-wire SPI), header
  pins 7 - 13 to GND, 3 and 6 open; VCC from 5 V (on 3V3 the panel stays dark).
  Keep leads under 15 cm with a ground beside them. Details in ws-displays.md.
  Title bars: green = firmware on main; blue = in the FSD, not built yet; orange = proposed, not in the FSD.

custom parts:
  Waveshare ESP32-S3-SIM7670G-4G: Waveshare ESP32-S3-SIM7670G-4G, header GPIOs of P2 and P3 in number order (not the physical order).
  4.2in e-Paper Module V2 SSD1683, 8-pin: Waveshare 4.2 inch e-Paper Module (V2), SSD1683
  3.12in OLED Ver 2.1 SSD1322, 4-wire SPI: 3.12 inch 256 x 64 OLED, SSD1322, module Ver 2.1 set for 4-wire SPI
