# Fritzing sketch wiring-8-ws-key (saved by Fritzing 1.0.0)

parts:
  Board = Waveshare ESP32-S3-SIM7670G-4G
  SW1 = Off-board key 12 mm, momentary, red LED
  R1 = Resistor 10k
  C1 = Capacitor 100 nF
  R2 = Resistor 1k
  R3 = Resistor 150R

nets:
  N1: Board.GND, SW1.3_NO, SW1.2_LED_-
  N2: Board.3V3, R1.1
  N3: Board.GND_R, C1.1
  N4: Board.IO12, R1.2, C1.2, R2.1
  N5: Board.IO13, R3.1
  N6: SW1.4_NO, R2.2
  N7: SW1.1_LED_+, R3.2

notes:
  Off-board key and its LED on the Waveshare board (FSD 35.2, FR-35.3, FR-35.18)
  Key: normally open, GPIO 12 to GND, active low; wakes the board from deep sleep.
  At the board end: R1 10k to 3V3, C1 100 nF to GND, R2 1k in series. Add a TVS
  diode from GPIO 12 to GND for a long cable (up to 3 m).
  LED: GPIO 13 (high = on) through R3 150R to LED +, LED - to GND; 68R at the least.
  Button pins: 3 and 4 (green leads) the switch, 1 (red) LED +, 2 (black) LED -.
  The header is unlabelled: find GPIO 12 and 13 with ws-probe's pin walk.
  Title bars: green = firmware on main; blue = in the FSD, not built yet; orange = proposed, not in the FSD.

custom parts:
  Waveshare ESP32-S3-SIM7670G-4G: Waveshare ESP32-S3-SIM7670G-4G, header GPIOs of P2 and P3 in number order (not the physical order).
  Off-board key 12 mm, momentary, red LED: 12 mm momentary push button, normally open, with a red LED
